// Logisim project 5Bit_Complemento2.circ as structural Verilog: 1 circuit, main circuit main
module main (
  input  [4:0] in_1,
  output [4:0] out_2
);

  wire [4:0] not_1_out;

  assign not_1_out = ~in_1;  // NOT_Gate not_1, 5 bits wide
  Adder #(.width(5)) adder_1 (.a(not_1_out), .b(5'b00001), .out(out_2));  // open: cin, cout
endmodule
