// Logisim project fpu.circ as structural Verilog: 5 circuits, main circuit main
module main (
  input  in_1,
  input  [7:0] in_2,
  input  [22:0] in_3,
  input  in_4,
  input  [7:0] in_5,
  input  [22:0] in_6,
  output [22:0] out_7,
  output [7:0] out_8
);

  wire ExpDiff_out_4;
  wire [7:0] AE, ExpDiff_out_3;
  wire [23:0] A1, A2;
  wire [26:0] Adder_sum_res;

  ExpDiff ExpDiff (.in_1(in_2), .in_2(in_5), .out_3(ExpDiff_out_3), .out_4(ExpDiff_out_4));
  Adder Adder (.A1(A1), .A2(A2), .SUM_RES(Adder_sum_res));  // open: COUT
  AuxAdapter Aux_Adapter (
    .E1(in_2), .N1(in_3), .E2(in_5), .N2(in_6), .POS(ExpDiff_out_4), .A1(A1), .EXPDIFF(ExpDiff_out_3),
    .AE(AE), .A2(A2));
  Normalizer Normalizer (.A1(Adder_sum_res), .EXP(AE), .out_3(out_7), .out_4(out_8));

  // Other names for the same wires on the sheet: N1E[7:0] = in_2; N1M[22:0] = in_3; N1S = in_1; N2E[7:0] = in_5;
  //   N2M[22:0] = in_6; N2S = in_4
endmodule

module ExpDiff (
  input  [7:0] in_1,
  input  [7:0] in_2,
  output [7:0] out_3,
  output out_4
);

  wire [7:0] main_1_out_2, subtractor_1_out;

  Subtractor subtractor_1 (.a(in_1), .b(in_2), .out(subtractor_1_out), .bout(out_4));  // open: bin
  _8Bit_Complemento2_main main_1 (.in_1(subtractor_1_out), .out_2(main_1_out_2));
  Multiplexer #(.width(8), .enable("false")) multiplexer_1 (
    .in0(subtractor_1_out), .in1(main_1_out_2), .out(out_3), .sel(out_4));
endmodule

module AuxAdapter (
  input  [7:0] E1,
  input  [22:0] N1,
  input  [7:0] E2,
  input  [22:0] N2,
  input  POS,
  input  [7:0] EXPDIFF,
  output [7:0] AE,
  output [23:0] A1,
  output [23:0] A2
);

  wire [4:0] bit_extender_2_out;
  wire [22:0] multiplexer_1_out, multiplexer_2_out;
  wire [23:0] bit_extender_3_out;

  Multiplexer #(.width(23), .enable("false")) multiplexer_1 (.in0(N1), .in1(N2), .out(multiplexer_1_out), .sel(POS));
  assign A1 = {{1{1'b1}}, multiplexer_1_out};  // Bit_Extender bit_extender_1
  Multiplexer #(.width(23), .enable("false")) multiplexer_2 (.in0(N2), .in1(N1), .out(multiplexer_2_out), .sel(POS));
  Multiplexer #(.width(8), .enable("false")) multiplexer_3 (.in0(E1), .in1(E2), .out(AE), .sel(POS));
  Bit_Extender #(.out_width(5), .\type ("one")) bit_extender_2 (.in(EXPDIFF), .out(bit_extender_2_out));
  assign bit_extender_3_out = {{1{1'b1}}, multiplexer_2_out};  // Bit_Extender bit_extender_3
  Shifter #(.width(24), .shift("lr")) shifter_1 (.in(bit_extender_3_out), .\dist (bit_extender_2_out), .out(A2));
endmodule

module Adder (
  input  [23:0] A1,
  input  [23:0] A2,
  output [26:0] SUM_RES,
  output COUT
);

  wire [26:0] bit_extender_1_out, bit_extender_2_out;

  assign bit_extender_1_out = {{3{1'b0}}, A1};  // Bit_Extender bit_extender_1
  assign bit_extender_2_out = {{3{1'b0}}, A2};  // Bit_Extender bit_extender_2
  Adder_part #(.width(27)) adder_1 (
    .a(bit_extender_1_out), .b(bit_extender_2_out), .out(SUM_RES), .cout(COUT));  // open: cin
endmodule

module Normalizer (
  input  [26:0] A1,
  input  [7:0] EXP,
  output [22:0] out_3,
  output [7:0] out_4
);

  wire NEG;
  wire [4:0] bitfinder_1_index, subtractor_1_out, subtractor_2_out;
  wire [7:0] adder_1_out, bit_extender_1_out, bit_extender_2_out, subtractor_3_out;
  wire [26:0] multiplexer_1_out, shifter_1_out, shifter_2_out;

  BitFinder #(.width(27), .\type ("high1")) bitfinder_1 (.in(A1), .index(bitfinder_1_index));  // open: found
  Subtractor #(.width(5)) subtractor_1 (
    .a(bitfinder_1_index), .b(5'b10111), .out(subtractor_1_out), .bout(NEG));  // open: bin
  Subtractor #(.width(5)) subtractor_2 (
    .a(5'b10111), .b(bitfinder_1_index), .out(subtractor_2_out));  // open: bin, bout
  assign bit_extender_1_out = {{3{1'b0}}, subtractor_1_out};  // Bit_Extender bit_extender_1
  assign bit_extender_2_out = {{3{1'b0}}, subtractor_2_out};  // Bit_Extender bit_extender_2
  Shifter #(.width(27), .shift("lr")) shifter_1 (.in(A1), .\dist (subtractor_1_out), .out(shifter_1_out));
  Shifter #(.width(27)) shifter_2 (.in(A1), .\dist (subtractor_2_out), .out(shifter_2_out));
  Adder_part adder_1 (.a(EXP), .b(bit_extender_1_out), .out(adder_1_out));  // open: cin, cout
  Subtractor subtractor_3 (.a(EXP), .b(bit_extender_2_out), .out(subtractor_3_out));  // open: bin, bout
  Multiplexer #(.width(27), .enable("false")) multiplexer_1 (
    .in0(shifter_1_out), .in1(shifter_2_out), .out(multiplexer_1_out), .sel(NEG));
  Bit_Extender #(.in_width(27), .out_width(23)) bit_extender_3 (.in(multiplexer_1_out), .out(out_3));
  Multiplexer #(.width(8), .enable("false")) multiplexer_2 (
    .in0(adder_1_out), .in1(subtractor_3_out), .out(out_4), .sel(NEG));
endmodule
